# Fritzing sketch assembly (saved by Fritzing 0.9.6b)
breadboards: 1

parts:
  Part1 = Adafruit Feather RP2040 [part_number="Adafruit #4884"]
  DFRobot_DFPlayer_Mini1 = DFRobot DFPlayer Mini [part_number=DFR0299]
  SP1 = SPEAKER [package=pcb_mount_speaker]
  Part2 = ws2812b [package="smd 2812b"]
  Part3 = ws2812b [package="smd 2812b"]
  Part4 = ws2812b [package="smd 2812b"]
  HC-SR04_Sensor_1 = HC-SR04 Ultrasonic Distance Sensor
  R1 = Resistor [tolerance=±5% power=0.25 resistance=22k package=THT]
  R2 = Resistor [tolerance=±5% power=0.25 resistance=33k package=THT]

nets:
  N1: Part1.TX, DFRobot_DFPlayer_Mini1.RX
  N2: Part1.MISO, R1.Pin_1, R2.Pin_0
  N3: Part1.MOSI, HC-SR04_Sensor_1.TRIG
  VSS: Part1.GND, DFRobot_DFPlayer_Mini1.GND-1, DFRobot_DFPlayer_Mini1.GND-2, Part2.VSS, Part3.VSS, Part4.VSS, HC-SR04_Sensor_1.GND, R2.Pin_1
  +3V3: Part1.+3V3, DFRobot_DFPlayer_Mini1.VCC
  N4: Part1.VUSB, HC-SR04_Sensor_1.VCC
  N5: Part1.D5, DFRobot_DFPlayer_Mini1.BUSY
  N6: Part1.SCL, Part4.DIN
  N7: DFRobot_DFPlayer_Mini1.SPK_1, SP1.-
  N8: DFRobot_DFPlayer_Mini1.SPK_2, SP1.+
  VDD: Part2.VDD, Part3.VDD
  N9: Part2.DIN, Part3.DOUT
  N10: Part3.DIN, Part4.DOUT
  N11: HC-SR04_Sensor_1.ECHO, R1.Pin_0

custom parts:
  Adafruit Feather RP2040: A new chip means a new Feather, and the Raspberry Pi RP2040 is no exception. When we saw this chip we thought "this chip is going to be awesome when we give it the Feather Treatment" and so we did! This Feather features the RP2040, and all niceties you know and love about Feather Measures 2.0" x 0.9" x 0.28" (50.8mm x 22.8mm x 7mm) without headers soldered in Light as a (large?) feather - 5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
